# Fritzing sketch 外置模块电路图 (saved by Fritzing 0.9.3b)
breadboards: 1

parts:
  Raspberry_Pi1 = Raspberry Pi B rev2  # not connected
  元件2 = Arduino Mega 2560 (Rev3)
  U1 = TRANSCHIPTC5747 [package=camera_sfv24r-2st_2]  # not connected
  S1 = Round Pushbutton  # not connected
  S2 = Round Pushbutton
  元件5 = Bluetooth HC-05 Macho
  LED1 = smd LED [color="Red (633nm)" package="1206 [SMD]"]  # not connected
  LED2 = smd LED [color="Red (633nm)" package="0805 [SMD]"]  # not connected
  LED3 = smd LED [color="Red (633nm)" package="0603 [SMD]"]  # not connected
  LED4 = smd LED [color="Red (633nm)" package="0603 [SMD]"]  # not connected
  LED5 = smd LED [color="Red (633nm)" package="0603 [SMD]"]  # not connected
  LED6 = smd LED [color="Red (633nm)" package="0805 [SMD]"]  # not connected
  R1 = Resistor [tolerance=±5% resistance=220 package=THT]  # not connected
  R3 = Resistor [tolerance=±5% resistance=220 package=THT]  # not connected
  R4 = Resistor [tolerance=±5% resistance=220 package=THT]  # not connected
  R5 = Resistor [tolerance=±5% resistance=220 package=THT]  # not connected
  R6 = Resistor [tolerance=±5% resistance=220 package=THT]  # not connected
  R7 = Resistor [tolerance=±5% resistance=220 package=THT]  # not connected
  LCD1 = LCD screen
  S3 = Round Pushbutton  # not connected

nets:
  N1: 元件2.A5, LCD1.V0
  N2: 元件2.A7, LCD1.RS
  N3: 元件2.D0_RX0, 元件5.TXD
  N4: 元件2.D1_TX0, 元件5.RXD
  N5: 元件2.D41, S2.leg0

notes:
  usb 摄像头
  usb通信
  5v 3A，稳流
  蓝牙模块，5v供电，可从拓展板取电，未画出。
  5v,拉高电压
  单片机控制按钮，拓展
  总电源按钮
  外置模块
  黑线GND共地，
  红线接io口，考虑电流功耗，可以接5v再连io。
  1602-i2c液晶显示,有驱动器，SDA对应A4,SCL对应A5。5v从拓展板取电，
  单片机备用按钮
  外置模块电路图
  1.按钮带自锁，且颜色不同。*3
  2.有些模块可从拓展版取电，取电连线未画出，拓展版直接覆盖再arduino mega 2560上。
  3.有些连线方式不知如何画出，故用文字代替。
