# Fritzing sketch 底盘原理图 (saved by Fritzing 0.9.3b)
breadboards: 1

parts:
  元件1 = Arduino Mega 2560 (Rev3)
  M1 = DC Motor
  M2 = DC Motor
  U1 = L298 [package=multiwatt15_6400bgheatsink]

nets:
  N1: 元件1.D9_PWM, U1.IN4
  N2: 元件1.D8_PWM, U1.IN3
  N3: 元件1.5V, U1.VLS
  GND: 元件1.GND, U1.GND
  N4: 元件1.D5_PWM, U1.IN1
  N5: 元件1.D6_PWM, U1.IN2
  N6: M1.pin_1, U1.OUT4
  N7: M1.pin_2, U1.OUT3
  N8: M2.pin_1, U1.OUT1
  N9: M2.pin_2, U1.OUT2

notes:
  编码器直流减速马达电机*2
  参数如下：12v-71rpm
  减速比 56
  功率 13w
  6根线，红黑蓝绿黄白、
  电机电源+，电机电源-
  编码器电5v+，编码器GND-
  编码器a相，编码器b相
  arduino mega2560
  中断引脚2&3,18&19
  注意编码器电源正负不要接错！
  12v取电
  底盘电路图
  1.连线注意正负问题，不要烧掉了。
  2.连线完毕后记得测试电机转向是否同向。
  3.取电方式请参考电源模块的图
  5v取电
